# Fritzing sketch group (saved by Fritzing 0.9.3b)
breadboards: 2

parts:
  Arduino_Uno = Arduino Uno (Rev3)
  Raspberry_Pi_1 = Raspberry Pi 3 [part_number=RPI-3-V1.2]
  R1 = Resistor [tolerance=±5% resistance=3.3k package=THT]
  R2 = Resistor [tolerance=±5% resistance=1.5k package=THT]
  R3 = Resistor [tolerance=±5% resistance=100 package=THT]
  S1 = Pushbutton [package="[THT]"]
  R4 = Resistor [tolerance=±5% resistance=10k package=THT]
  R5 = Resistor [tolerance=±5% resistance=220 package=THT]
  LED1 = LED - 5mm [color="Red (633nm)" package="5 mm [THT]"]

nets:
  N1: Arduino_Uno.D8, R5.Pin_1
  GND: Arduino_Uno.GND, Raspberry_Pi_1.GND, R1.Pin_0, R4.Pin_1, LED1.cathode
  N2: Arduino_Uno.D0/RX, Raspberry_Pi_1.GIPO14
  N3: Arduino_Uno.D1/TX, R2.Pin_0
  N4: Arduino_Uno.D7, S1.Pin_1, S1.Pin_2, R4.Pin_0
  N5: Arduino_Uno.5V, S1.Pin_3, S1.Pin_4
  N6: Raspberry_Pi_1.GIPO15, R1.Pin_1, R3.Pin_1
  N7: R2.Pin_1, R3.Pin_0
  N8: R5.Pin_0, LED1.anode
